// Logisim project ALU.circ as structural Verilog: 1 circuit, main circuit main
module main (
  input  [31:0] A,
  input  [31:0] B,
  input  [3:0] ALUSel,
  output [31:0] Result,
  output OverFlow,
  output Zero
);
endmodule
