// Logisim project Adder.circ as structural Verilog: 14 circuits, main circuit 32bitAdder
// 4bitCL
module _4bitCLA (
  input  cin,
  input  P1,
  input  G1,
  input  P2,
  input  G2,
  input  P3,
  input  G3,
  input  P4,
  input  G4,
  output p_prime,
  output g_prime,
  output c1,
  output c2,
  output c3,
  output c4,
  output c5
);

  wire and_2_out, and_3_out, or_1_out, or_2_out, P1cin_out, P2c2_out, p2g1_out, P3c3_out, P4c4_out;

  and and_1 (p_prime, P4, P3, P2, P1);
  and p2g1 (p2g1_out, G1, P2);
  and P1cin (P1cin_out, cin, P1);
  or or_1 (or_1_out, p2g1_out, G2);
  or u_c2 (c2, P1cin_out, G1);
  and and_2 (and_2_out, or_1_out, or_1_out, P3);
  and P2c2 (P2c2_out, c2, P2);
  or or_2 (or_2_out, and_2_out, G3);
  or u_c3 (c3, P2c2_out, G2);
  and and_3 (and_3_out, or_2_out, P4);
  and P3c3 (P3c3_out, c3, P3);
  or or_3 (g_prime, and_3_out, G4);
  or u_c4 (c4, P3c3_out, G3);
  and P4c4 (P4c4_out, c4, P4);
  or u_c5 (c5, P4c4_out, G4);

  assign c1 = cin;
endmodule

module _4bitSum (
  input  c0,
  input  p1,
  input  c1,
  input  p2,
  input  c2,
  input  p3,
  input  c3,
  input  p4,
  output s1,
  output s2,
  output s3,
  output s4
);

  xor xor_1 (s1, c0, p1);
  xor xor_2 (s2, c1, p2);
  xor xor_3 (s3, c2, p3);
  xor xor_4 (s4, c3, p4);
endmodule

module PG (
  input  x1,
  input  y1,
  input  x2,
  input  y2,
  input  x3,
  input  y3,
  input  x4,
  input  y4,
  output p1,
  output g1,
  output p2,
  output g2,
  output p3,
  output g3,
  output p4,
  output g4
);

  xor xor_1 (p1, x1, y1);
  and and_1 (g1, x1, y1);
  xor xor_2 (p2, x2, y2);
  and and_2 (g2, x2, y2);
  xor xor_3 (p3, x3, y3);
  and and_3 (g3, x3, y3);
  xor xor_4 (p4, x4, y4);
  and and_4 (g4, x4, y4);
endmodule

// 16bitAdd
module _16bitAdder (
  input  Cin,
  input  [15:0] B,
  input  [15:0] A,
  output [15:0] Result,
  output over
);

  wire n4bitadder_1_g_prime, n4bitadder_1_p_prime, n4bitadder_2_g_prime, n4bitadder_2_p_prime,
       n4bitadder_3_g_prime, n4bitadder_3_p_prime, n4bitadder_4_g_prime, n4bitadder_4_p_prime, n4bitcla_1_c2,
       n4bitcla_1_c3, n4bitcla_1_c4;

  _4bitAdder u_4bitadder_1 (
    .a1(A[0]), .b1(B[0]), .a2(A[1]), .b2(B[1]), .a3(A[2]), .b3(B[2]), .a4(A[3]), .b4(B[3]), .c1(Cin),
    .p_prime(n4bitadder_1_p_prime), .g_prime(n4bitadder_1_g_prime), .s1(Result[0]), .s2(Result[1]),
    .s3(Result[2]), .s4(Result[3]));  // open: s5
  _4bitAdder u_4bitadder_2 (
    .a1(A[4]), .b1(B[4]), .a2(A[5]), .b2(B[5]), .a3(A[6]), .b3(B[6]), .a4(A[7]), .b4(B[7]),
    .c1(n4bitcla_1_c2), .p_prime(n4bitadder_2_p_prime), .g_prime(n4bitadder_2_g_prime), .s1(Result[4]),
    .s2(Result[5]), .s3(Result[6]), .s4(Result[7]));  // open: s5
  _4bitAdder u_4bitadder_3 (
    .a1(A[8]), .b1(B[8]), .a2(A[9]), .b2(B[9]), .a3(A[10]), .b3(B[10]), .a4(A[11]), .b4(B[11]),
    .c1(n4bitcla_1_c3), .p_prime(n4bitadder_3_p_prime), .g_prime(n4bitadder_3_g_prime), .s1(Result[8]),
    .s2(Result[9]), .s3(Result[10]), .s4(Result[11]));  // open: s5
  _4bitAdder u_4bitadder_4 (
    .a1(A[12]), .b1(B[12]), .a2(A[13]), .b2(B[13]), .a3(A[14]), .b3(B[14]), .a4(A[15]), .b4(B[15]),
    .c1(n4bitcla_1_c4), .p_prime(n4bitadder_4_p_prime), .g_prime(n4bitadder_4_g_prime), .s1(Result[12]),
    .s2(Result[13]), .s3(Result[14]), .s4(Result[15]));  // open: s5
  _4bitCLA u_4bitcla_1 (
    .cin(Cin), .P1(n4bitadder_1_p_prime), .G1(n4bitadder_1_g_prime), .P2(n4bitadder_2_p_prime),
    .G2(n4bitadder_2_g_prime), .P3(n4bitadder_3_p_prime), .G3(n4bitadder_3_g_prime),
    .P4(n4bitadder_4_p_prime), .G4(n4bitadder_4_g_prime), .c2(n4bitcla_1_c2), .c3(n4bitcla_1_c3),
    .c4(n4bitcla_1_c4), .c5(over));  // open: p_prime, g_prime, c1
endmodule

// 4bitAdd
module _4bitAdder (
  input  c1,
  input  a1,
  input  b1,
  input  a2,
  input  b2,
  input  a3,
  input  b3,
  input  a4,
  input  b4,
  output p_prime,
  output g_prime,
  output s1,
  output s2,
  output s3,
  output s4,
  output s5
);

  wire n4bitcla_1_c1, n4bitcla_1_c2, n4bitcla_1_c3, n4bitcla_1_c4, pg_1_g1, pg_1_g2, pg_1_g3, pg_1_g4,
       pg_1_p1, pg_1_p2, pg_1_p3, pg_1_p4;

  PG pg_1 (
    .x1(a1), .y1(b1), .x2(a2), .y2(b2), .x3(a3), .y3(b3), .x4(a4), .y4(b4), .p1(pg_1_p1), .g1(pg_1_g1),
    .p2(pg_1_p2), .g2(pg_1_g2), .p3(pg_1_p3), .g3(pg_1_g3), .p4(pg_1_p4), .g4(pg_1_g4));
  PG pg_2 (
    .x1(a1), .y1(b1), .x2(a2), .y2(b2), .x3(a3), .y3(b3), .x4(a4), .y4(b4), .p1(pg_1_p1), .g1(pg_1_g1),
    .p2(pg_1_p2), .g2(pg_1_g2), .p3(pg_1_p3), .g3(pg_1_g3), .p4(pg_1_p4), .g4(pg_1_g4));
  _4bitCLA u_4bitcla_1 (
    .cin(c1), .P1(pg_1_p1), .G1(pg_1_g1), .P2(pg_1_p2), .G2(pg_1_g2), .P3(pg_1_p3), .G3(pg_1_g3),
    .P4(pg_1_p4), .G4(pg_1_g4), .p_prime(p_prime), .g_prime(g_prime), .c1(n4bitcla_1_c1), .c2(n4bitcla_1_c2),
    .c3(n4bitcla_1_c3), .c4(n4bitcla_1_c4), .c5(s5));
  _4bitSum u_4bitsum_1 (
    .c0(n4bitcla_1_c1), .p1(pg_1_p1), .c1(n4bitcla_1_c2), .p2(pg_1_p2), .c2(n4bitcla_1_c3), .p3(pg_1_p3),
    .c3(n4bitcla_1_c4), .p4(pg_1_p4), .s1(s1), .s2(s2), .s3(s3), .s4(s4));
endmodule

// add
module _32bitAdder (
  input  [31:0] A,
  input  [31:0] B,
  output [31:0] Result,
  output OverFlow
);

  wire n16bitadder_1_over;

  _16bitAdder u_16bitadder_1 (.Cin(1'b0), .B(A[15:0]), .A(B[15:0]), .Result(Result[15:0]), .over(n16bitadder_1_over));
  _16bitAdder u_16bitadder_2 (
    .Cin(n16bitadder_1_over), .B(A[31:16]), .A(B[31:16]), .Result(Result[31:16]), .over(OverFlow));
endmodule

module alu (
  input  [31:0] A,
  input  [31:0] B,
  input  [3:0] ALUSel,
  output Zero,
  output OverFlow,
  output [31:0] Result
);

  wire comparator_1_lt, comparator_2_eq, decoder_1_out0, decoder_1_out1, decoder_1_out2, decoder_1_out4,
       decoder_1_out5, decoder_1_out6, decoder_1_out7, decoder_1_out8, decoder_1_out9, decoder_1_out12,
       decoder_1_out15;
  wire [31:0] add_result, and_1_out, and_2_out, and_3_out, and_4_out, and_5_out, and_6_out, and_7_out,
       and_8_out, and_9_out, and_10_out, and_11_out, and_12_out, and_13_out, and_14_out, and_15_out,
       and_16_out, and_17_out, and_18_out, and_19_out, and_20_out, and_21_out, and_22_result,
       bit_extender_1_out, bit_extender_2_out, bit_extender_3_out, bit_extender_4_out, bit_extender_5_out,
       bit_extender_6_out, bit_extender_7_out, bit_extender_8_out, bit_extender_9_out, bit_extender_10_out,
       bit_extender_11_out, bit_extender_12_out, multh_1_result, multiplier_1_out, n32bitor_1_result,
       n32bitor_2_result, n32bitor_3_result, n32bitor_4_result, n32bitor_5_result, n32bitor_6_result,
       n32bitor_7_result, n32bitor_8_result, n32bitor_9_result, or_result, shifter_left_1_result,
       shifter_right_1_result, subtractor_1_out, xor_result;

  Decoder #(.select(4), .enable("false")) decoder_1 (
    .out0(decoder_1_out0), .out1(decoder_1_out1), .out2(decoder_1_out2), .out4(decoder_1_out4),
    .out5(decoder_1_out5), .out6(decoder_1_out6), .out7(decoder_1_out7), .out8(decoder_1_out8),
    .out9(decoder_1_out9), .out12(decoder_1_out12), .out15(decoder_1_out15), .sel(ALUSel));  // open: out3, out10, out11, out13, out14
  assign bit_extender_1_out = {{31{decoder_1_out5}}, decoder_1_out5};  // Bit_Extender bit_extender_1
  assign bit_extender_2_out = {{31{decoder_1_out2}}, decoder_1_out2};  // Bit_Extender bit_extender_2
  assign bit_extender_3_out = {{31{decoder_1_out0}}, decoder_1_out0};  // Bit_Extender bit_extender_3
  assign bit_extender_4_out = {{31{decoder_1_out6}}, decoder_1_out6};  // Bit_Extender bit_extender_4
  assign bit_extender_5_out = {{31{decoder_1_out12}}, decoder_1_out12};  // Bit_Extender bit_extender_5
  assign bit_extender_6_out = {{31{decoder_1_out9}}, decoder_1_out9};  // Bit_Extender bit_extender_6
  assign bit_extender_7_out = {{31{decoder_1_out15}}, decoder_1_out15};  // Bit_Extender bit_extender_7
  assign bit_extender_8_out = {{31{decoder_1_out4}}, decoder_1_out4};  // Bit_Extender bit_extender_8
  assign bit_extender_9_out = {{31{decoder_1_out8}}, decoder_1_out8};  // Bit_Extender bit_extender_9
  assign bit_extender_10_out = {{31{decoder_1_out7}}, decoder_1_out7};  // Bit_Extender bit_extender_10
  assign bit_extender_11_out = {{31{decoder_1_out1}}, decoder_1_out1};  // Bit_Extender bit_extender_11
  assign and_1_out = A & bit_extender_8_out;  // AND_Gate and_1, 32 bits wide
  assign and_2_out = B & bit_extender_8_out;  // AND_Gate and_2, 32 bits wide
  assign and_3_out = A & bit_extender_1_out;  // AND_Gate and_3, 32 bits wide
  assign and_4_out = bit_extender_1_out & B;  // AND_Gate and_4, 32 bits wide
  assign and_5_out = A & bit_extender_2_out;  // AND_Gate and_5, 32 bits wide
  assign and_6_out = bit_extender_2_out & B;  // AND_Gate and_6, 32 bits wide
  assign and_7_out = A & bit_extender_3_out;  // AND_Gate and_7, 32 bits wide
  assign and_8_out = B & bit_extender_3_out;  // AND_Gate and_8, 32 bits wide
  assign and_9_out = bit_extender_11_out & A;  // AND_Gate and_9, 32 bits wide
  assign and_10_out = bit_extender_11_out & B;  // AND_Gate and_10, 32 bits wide
  assign and_11_out = B & bit_extender_9_out;  // AND_Gate and_11, 32 bits wide
  assign and_12_out = bit_extender_6_out & A;  // AND_Gate and_12, 32 bits wide
  assign and_13_out = A & bit_extender_4_out;  // AND_Gate and_13, 32 bits wide
  assign and_14_out = B & bit_extender_4_out;  // AND_Gate and_14, 32 bits wide
  assign and_15_out = A & bit_extender_10_out;  // AND_Gate and_15, 32 bits wide
  assign and_16_out = B & bit_extender_10_out;  // AND_Gate and_16, 32 bits wide
  assign and_17_out = A & bit_extender_5_out;  // AND_Gate and_17, 32 bits wide
  assign and_18_out = B & bit_extender_5_out;  // AND_Gate and_18, 32 bits wide
  assign and_19_out = B & bit_extender_7_out;  // AND_Gate and_19, 32 bits wide
  Shifter_Right shifter_right_1 (.A(and_3_out), .B(and_4_out), .Result(shifter_right_1_result));
  _32bitAdder add (.A(and_7_out), .B(and_8_out), .Result(add_result), .OverFlow(OverFlow));
  assign and_20_out = A & bit_extender_9_out;  // AND_Gate and_20, 32 bits wide
  _32bitXOR \xor  (.A(and_1_out), .B(and_2_out), .Result(xor_result));
  Multh multh_1 (.A(and_12_out), .B(and_21_out), .Result(multh_1_result));
  assign and_21_out = bit_extender_6_out & B;  // AND_Gate and_21, 32 bits wide
  _32bitOR \or  (.A(and_13_out), .B(and_14_out), .Result(or_result));
  _32bitAND and_22 (.A(and_15_out), .B(and_16_out), .Result(and_22_result));
  Subtractor #(.width(32)) subtractor_1 (.a(and_17_out), .b(and_18_out), .out(subtractor_1_out));  // open: bin, bout
  Comparator #(.width(32), .mode("unsigned")) comparator_1 (
    .a(and_5_out), .b(and_6_out), .lt(comparator_1_lt));  // open: gt, eq
  assign bit_extender_12_out = {{31{1'b0}}, comparator_1_lt};  // Bit_Extender bit_extender_12
  Shifter_Left shifter_left_1 (.A(and_9_out), .B(and_10_out), .Result(shifter_left_1_result));
  Multiplier #(.width(32)) multiplier_1 (.a(and_20_out), .b(and_11_out), .out(multiplier_1_out));  // open: cin, cout
  _32bitOR u_32bitor_1 (.A(subtractor_1_out), .B(and_19_out), .Result(n32bitor_1_result));
  _32bitOR u_32bitor_2 (.A(n32bitor_7_result), .B(add_result), .Result(n32bitor_2_result));
  _32bitOR u_32bitor_3 (.A(shifter_left_1_result), .B(n32bitor_8_result), .Result(n32bitor_3_result));
  _32bitOR u_32bitor_4 (.A(multh_1_result), .B(n32bitor_5_result), .Result(n32bitor_4_result));
  _32bitOR u_32bitor_5 (.A(or_result), .B(n32bitor_6_result), .Result(n32bitor_5_result));
  _32bitOR u_32bitor_6 (.A(and_22_result), .B(n32bitor_1_result), .Result(n32bitor_6_result));
  _32bitOR u_32bitor_7 (.A(shifter_right_1_result), .B(bit_extender_12_out), .Result(n32bitor_7_result));
  _32bitOR u_32bitor_8 (.A(multiplier_1_out), .B(n32bitor_9_result), .Result(n32bitor_8_result));
  _32bitOR u_32bitor_9 (.A(xor_result), .B(n32bitor_4_result), .Result(n32bitor_9_result));
  _32bitOR u_32bitor_10 (.A(n32bitor_2_result), .B(n32bitor_3_result), .Result(Result));
  Multiplexer #(.disabled(0), .enable("false")) multiplexer_1 (
    .in0(1'b0), .in1(1'b1), .out(Zero), .sel(comparator_2_eq));
  Comparator #(.width(32), .mode("unsigned")) comparator_2 (
    .a({32{1'b0}}), .b(Result), .eq(comparator_2_eq));  // open: gt, lt
endmodule

// or
module _32bitOR (
  input  [31:0] A,
  input  [31:0] B,
  output [31:0] Result
);

  or _23 (Result[23], A[23], B[23]);
  or _22 (Result[22], A[22], B[22]);
  or _21 (Result[21], A[21], B[21]);
  or _20 (Result[20], A[20], B[20]);
  or _19 (Result[19], A[19], B[19]);
  or _18 (Result[18], A[18], B[18]);
  or _17 (Result[17], A[17], B[17]);
  or _16 (Result[16], A[16], B[16]);
  or _14 (Result[14], A[14], B[14]);
  or _15 (Result[15], A[15], B[15]);
  or _12 (Result[12], A[12], B[12]);
  or _13 (Result[13], A[13], B[13]);
  or _11 (Result[11], A[11], B[11]);
  or _24 (Result[24], A[31], B[24]);
  or _9 (Result[9], A[9], B[9]);
  or _10 (Result[10], A[10], B[10]);
  or _25 (Result[25], A[30], B[25]);
  or _26 (Result[26], A[29], B[26]);
  or _8 (Result[8], A[8], B[8]);
  or _27 (Result[27], A[28], B[27]);
  or _28 (Result[28], A[27], B[28]);
  or _6 (Result[6], A[6], B[6]);
  or _7 (Result[7], A[7], B[7]);
  or _29 (Result[29], A[26], B[29]);
  or _5 (Result[5], A[5], B[5]);
  or _30 (Result[30], A[25], B[30]);
  or _31 (Result[31], A[24], B[31]);
  or _3 (Result[3], A[3], B[3]);
  or _4 (Result[4], A[4], B[4]);
  or _1 (Result[1], A[1], B[1]);
  or _2 (Result[2], A[2], B[2]);
  or _0 (Result[0], A[0], B[0]);
endmodule

module _32bitAND (
  input  [31:0] A,
  input  [31:0] B,
  output [31:0] Result
);

  and and_1 (Result[23], A[23], B[23]);
  and and_2 (Result[22], A[22], B[22]);
  and and_3 (Result[21], A[21], B[21]);
  and and_4 (Result[20], A[20], B[20]);
  and and_5 (Result[19], A[19], B[19]);
  and and_6 (Result[18], A[18], B[18]);
  and and_7 (Result[17], A[17], B[17]);
  and and_8 (Result[16], A[16], B[16]);
  and and_9 (Result[14], A[14], B[14]);
  and and_10 (Result[15], A[15], B[15]);
  and and_11 (Result[12], A[12], B[12]);
  and and_12 (Result[13], A[13], B[13]);
  and and_13 (Result[11], A[11], B[11]);
  and and_14 (Result[24], A[31], B[24]);
  and and_15 (Result[9], A[9], B[9]);
  and and_16 (Result[10], A[10], B[10]);
  and and_17 (Result[25], A[30], B[25]);
  and and_18 (Result[26], A[29], B[26]);
  and and_19 (Result[8], A[8], B[8]);
  and and_20 (Result[27], A[28], B[27]);
  and and_21 (Result[28], A[27], B[28]);
  and and_22 (Result[6], A[6], B[6]);
  and and_23 (Result[7], A[7], B[7]);
  and and_24 (Result[29], A[26], B[29]);
  and and_25 (Result[5], A[5], B[5]);
  and and_26 (Result[30], A[25], B[30]);
  and and_27 (Result[31], A[24], B[31]);
  and and_28 (Result[3], A[3], B[3]);
  and and_29 (Result[4], A[4], B[4]);
  and and_30 (Result[1], A[1], B[1]);
  and and_31 (Result[2], A[2], B[2]);
  and and_32 (Result[0], A[0], B[0]);
endmodule

module _32bitXOR (
  input  [31:0] A,
  input  [31:0] B,
  output [31:0] Result
);

  xor xor_1 (Result[23], A[23], B[23]);
  xor xor_2 (Result[22], A[22], B[22]);
  xor xor_3 (Result[21], A[21], B[21]);
  xor xor_4 (Result[20], A[20], B[20]);
  xor xor_5 (Result[19], A[19], B[19]);
  xor xor_6 (Result[18], A[18], B[18]);
  xor xor_7 (Result[17], A[17], B[17]);
  xor xor_8 (Result[16], A[16], B[16]);
  xor xor_9 (Result[14], A[14], B[14]);
  xor xor_10 (Result[15], A[15], B[15]);
  xor xor_11 (Result[12], A[12], B[12]);
  xor xor_12 (Result[13], A[13], B[13]);
  xor xor_13 (Result[11], A[11], B[11]);
  xor xor_14 (Result[24], A[31], B[24]);
  xor xor_15 (Result[9], A[9], B[9]);
  xor xor_16 (Result[10], A[10], B[10]);
  xor xor_17 (Result[25], A[30], B[25]);
  xor xor_18 (Result[26], A[29], B[26]);
  xor xor_19 (Result[8], A[8], B[8]);
  xor xor_20 (Result[27], A[28], B[27]);
  xor xor_21 (Result[28], A[27], B[28]);
  xor xor_22 (Result[6], A[6], B[6]);
  xor xor_23 (Result[7], A[7], B[7]);
  xor xor_24 (Result[29], A[26], B[29]);
  xor xor_25 (Result[5], A[5], B[5]);
  xor xor_26 (Result[30], A[25], B[30]);
  xor xor_27 (Result[31], A[24], B[31]);
  xor xor_28 (Result[3], A[3], B[3]);
  xor xor_29 (Result[4], A[4], B[4]);
  xor xor_30 (Result[1], A[1], B[1]);
  xor xor_31 (Result[2], A[2], B[2]);
  xor xor_32 (Result[0], A[0], B[0]);
endmodule

module Mult (
  input  [31:0] A,
  input  [31:0] B,
  output [31:0] Result
);

  Multiplier #(.width(32)) multiplier_1 (.a(A), .b(B), .out(Result));  // open: cin, cout
endmodule

module Multh (
  input  [31:0] A,
  input  [31:0] B,
  output [31:0] Result
);

  wire [31:0] bit_extender_1_out, bit_extender_2_out, bit_extender_3_out, bit_extender_4_out,
       bit_extender_5_out, bit_extender_6_out, bit_extender_7_out, bit_extender_8_out, multiplier_1_out,
       multiplier_2_out, multiplier_3_out, n32bitadder_1_result;

  assign bit_extender_1_out = {{16{1'b0}}, A[15:0]};  // Bit_Extender bit_extender_1
  assign bit_extender_2_out = {{16{1'b0}}, B[31:16]};  // Bit_Extender bit_extender_2
  assign bit_extender_3_out = {{16{1'b0}}, B[15:0]};  // Bit_Extender bit_extender_3
  assign bit_extender_4_out = {{16{1'b0}}, A[31:16]};  // Bit_Extender bit_extender_4
  assign bit_extender_5_out = {{16{1'b0}}, B[31:16]};  // Bit_Extender bit_extender_5
  assign bit_extender_6_out = {{16{1'b0}}, A[31:16]};  // Bit_Extender bit_extender_6
  Multiplier #(.width(32)) multiplier_1 (
    .a(bit_extender_1_out), .b(bit_extender_2_out), .out(multiplier_1_out));  // open: cin, cout
  Multiplier #(.width(32)) multiplier_2 (
    .a(bit_extender_3_out), .b(bit_extender_4_out), .out(multiplier_2_out));  // open: cin, cout
  Multiplier #(.width(32)) multiplier_3 (
    .a(bit_extender_5_out), .b(bit_extender_6_out), .out(multiplier_3_out));  // open: cin, cout
  assign bit_extender_7_out = {{16{1'b0}}, multiplier_1_out[31:16]};  // Bit_Extender bit_extender_7
  assign bit_extender_8_out = {{16{1'b0}}, multiplier_2_out[31:16]};  // Bit_Extender bit_extender_8
  _32bitAdder u_32bitadder_1 (
    .A(bit_extender_7_out), .B(bit_extender_8_out), .Result(n32bitadder_1_result));  // open: OverFlow
  _32bitAdder u_32bitadder_2 (.A(n32bitadder_1_result), .B(multiplier_3_out), .Result(Result));  // open: OverFlow
endmodule

module Shifter_Left (
  input  [31:0] A,
  input  [31:0] B,
  output [31:0] Result
);

  wire comparator_1_lt;
  wire [4:0] bit_extender_1_out;
  wire [31:0] bit_extender_2_out, shifter_1_out;

  Bit_Extender #(.in_width(32), .out_width(5), .\type ("sign")) bit_extender_1 (.in(B), .out(bit_extender_1_out));
  Comparator #(.width(32), .mode("unsigned")) comparator_1 (.a(B), .b(32'h20), .lt(comparator_1_lt));  // open: gt, eq
  Shifter #(.width(32)) shifter_1 (.in(A), .\dist (bit_extender_1_out), .out(shifter_1_out));
  assign bit_extender_2_out = {{31{comparator_1_lt}}, comparator_1_lt};  // Bit_Extender bit_extender_2
  assign Result = shifter_1_out & bit_extender_2_out;  // AND_Gate and_1, 32 bits wide
endmodule

module Shifter_Right (
  input  [31:0] A,
  input  [31:0] B,
  output [31:0] Result
);

  wire comparator_1_lt;
  wire [4:0] bit_extender_1_out;
  wire [31:0] bit_extender_2_out, shifter_1_out;

  Bit_Extender #(.in_width(32), .out_width(5), .\type ("sign")) bit_extender_1 (.in(B), .out(bit_extender_1_out));
  Comparator #(.width(32), .mode("unsigned")) comparator_1 (.a(B), .b(32'h20), .lt(comparator_1_lt));  // open: gt, eq
  Shifter #(.width(32), .shift("lr")) shifter_1 (.in(A), .\dist (bit_extender_1_out), .out(shifter_1_out));
  assign bit_extender_2_out = {{31{comparator_1_lt}}, comparator_1_lt};  // Bit_Extender bit_extender_2
  assign Result = shifter_1_out & bit_extender_2_out;  // AND_Gate and_1, 32 bits wide
endmodule
